# Fritzing sketch matrix_keypad (saved by Fritzing 0.7.10b)
breadboards: 1

parts:
  pyMCU_v1_1 = pyMCU
  KEYPAD1 = Membrane Matrix Keypad
  R1 = Resistor [tolerance=±5% resistance=10k package=THT]
  R2 = Resistor [tolerance=±5% resistance=10k package=THT]

nets:
  N1: pyMCU_v1_1.VCC, R1.Pin_1, R2.Pin_1
  N2: KEYPAD1.1, R1.Pin_0
  N3: KEYPAD1.2, R2.Pin_0

custom parts:
  pyMCU: pyMCU - Python Controlled Microcontroller http://www.pymcu.com
  Membrane Matrix Keypad: Membrane Matrix 3x4 Keypad
